// Logisim project Project 32.circ as structural Verilog: 5 circuits, main circuit main
module main (
  input  in_1,
  input  in_2,
  input  [31:0] in_3,
  output [31:0] out_4,
  output [31:0] out_5
);

  wire alu_1_out_5, and_1_out, clock_1_out, control_unit_1_out_2, control_unit_1_out_3, control_unit_1_out_4,
       control_unit_1_out_5, control_unit_1_out_6, control_unit_1_out_7;
  wire [1:0] control_unit_1_out_8;
  wire [3:0] alu_ctrl_1_alu_sl;
  wire [7:0] adder_1_out, bit_extender_1_out, bit_extender_3_out, multiplexer_1_out, register_1_q;
  wire [31:0] alu_1_out_4, bit_extender_2_out, multiplexer_2_out, ram_2_data, reg_file_1_out_7;

  Clock clock_1 (.out(clock_1_out));
  Bit_Extender #(.in_width(12), .out_width(8)) bit_extender_1 (.in(in_3[31:20]), .out(bit_extender_1_out));
  Adder adder_1 (.a(8'h1), .b(register_1_q), .out(adder_1_out));  // open: cin, cout
  Register register_1 (.D(multiplexer_1_out), .Q(register_1_q), .clk(clock_1_out), .clr(in_1));  // open: en
  Multiplexer #(.width(8)) multiplexer_1 (
    .in0(adder_1_out), .in1(bit_extender_1_out), .out(multiplexer_1_out), .sel(and_1_out));  // open: en
  RAM #(.dataWidth(32), .bus("separate")) ram_1 (
    .addr(register_1_q), .sel(1'b1), .clk(clock_1_out), .ld(1'b1), .clr(in_2));  // open: din, data, str
  and and_1 (and_1_out, control_unit_1_out_7, alu_1_out_5);
  Control_Unit control_unit_1 (
    .in_1(in_3[6:0]), .out_2(control_unit_1_out_2), .out_3(control_unit_1_out_3),
    .out_4(control_unit_1_out_4), .out_5(control_unit_1_out_5), .out_6(control_unit_1_out_6),
    .out_7(control_unit_1_out_7), .out_8(control_unit_1_out_8));
  assign bit_extender_2_out = {{20{1'b0}}, in_3[31:20]};  // Bit_Extender bit_extender_2
  Reg_File reg_file_1 (
    .in_1(control_unit_1_out_3), .in_2(clock_1_out), .WB(out_5), .RS_1(in_3[19:15]), .RD(in_3[11:7]),
    .RS_2(in_3[24:20]), .out_7(reg_file_1_out_7), .out_8(out_4));
  Multiplexer #(.width(32)) multiplexer_2 (
    .in0(out_4), .in1(bit_extender_2_out), .out(multiplexer_2_out), .sel(control_unit_1_out_2));  // open: en
  ALU_CTRL alu_ctrl_1 (
    .Function_7(in_3[31:25]), .Function_3(in_3[14:12]), .Input(control_unit_1_out_8),
    .ALU_SL(alu_ctrl_1_alu_sl));
  ALU alu_1 (
    .in_3(alu_ctrl_1_alu_sl), .in_1(reg_file_1_out_7), .in_2(multiplexer_2_out), .out_4(alu_1_out_4),
    .out_5(alu_1_out_5));
  Bit_Extender #(.in_width(32), .out_width(8)) bit_extender_3 (.in(reg_file_1_out_7), .out(bit_extender_3_out));
  RAM #(.dataWidth(32), .bus("separate")) ram_2 (
    .addr(bit_extender_3_out), .din(out_4), .data(ram_2_data), .str(control_unit_1_out_6), .sel(1'b1),
    .clk(clock_1_out), .ld(control_unit_1_out_5));  // open: clr
  Multiplexer #(.width(32)) multiplexer_3 (
    .in0(alu_1_out_4), .in1(ram_2_data), .out(out_5), .sel(control_unit_1_out_4));  // open: en
endmodule

module Reg_File (
  input  in_1,
  input  in_2,
  input  [31:0] WB,
  input  [4:0] RS_1,
  input  [4:0] RD,
  input  [4:0] RS_2,
  output [31:0] out_7,
  output [31:0] out_8
);

  wire and_2_out, and_3_out, and_4_out, and_5_out, and_6_out, and_7_out, and_8_out, and_9_out, and_10_out,
       and_11_out, and_12_out, and_13_out, and_14_out, and_15_out, and_16_out, and_17_out, and_18_out,
       and_19_out, and_20_out, and_21_out, and_22_out, and_23_out, and_24_out, and_25_out, and_26_out,
       and_27_out, and_28_out, and_29_out, and_30_out, and_31_out, and_32_out, and_33_out, CLK,
       decoder_1_out0, decoder_1_out1, decoder_1_out2, decoder_1_out3, decoder_1_out4, decoder_1_out5,
       decoder_1_out6, decoder_1_out7, decoder_1_out8, decoder_1_out9, decoder_1_out10, decoder_1_out11,
       decoder_1_out12, decoder_1_out13, decoder_1_out14, decoder_1_out15, decoder_1_out16, decoder_1_out17,
       decoder_1_out18, decoder_1_out19, decoder_1_out20, decoder_1_out21, decoder_1_out22, decoder_1_out23,
       decoder_1_out24, decoder_1_out25, decoder_1_out26, decoder_1_out27, decoder_1_out28, decoder_1_out29,
       decoder_1_out30, decoder_1_out31, undriven;
  wire [31:0] register_1_q, register_2_q, register_3_q, register_4_q, register_5_q, register_6_q,
       register_7_q, register_8_q, register_9_q, register_10_q, register_11_q, register_12_q, register_13_q,
       register_14_q, register_15_q, register_16_q, register_17_q, register_18_q, register_19_q,
       register_20_q, register_21_q, register_22_q, register_23_q, register_24_q, register_25_q,
       register_26_q, register_27_q, register_28_q, register_29_q, register_30_q, register_31_q,
       register_32_q;

  and and_1 (CLK, in_1, in_2);
  Decoder #(.select(5)) decoder_1 (
    .out0(decoder_1_out0), .out1(decoder_1_out1), .out2(decoder_1_out2), .out3(decoder_1_out3),
    .out4(decoder_1_out4), .out5(decoder_1_out5), .out6(decoder_1_out6), .out7(decoder_1_out7),
    .out8(decoder_1_out8), .out9(decoder_1_out9), .out10(decoder_1_out10), .out11(decoder_1_out11),
    .out12(decoder_1_out12), .out13(decoder_1_out13), .out14(decoder_1_out14), .out15(decoder_1_out15),
    .out16(decoder_1_out16), .out17(decoder_1_out17), .out18(decoder_1_out18), .out19(decoder_1_out19),
    .out20(decoder_1_out20), .out21(decoder_1_out21), .out22(decoder_1_out22), .out23(decoder_1_out23),
    .out24(decoder_1_out24), .out25(decoder_1_out25), .out26(decoder_1_out26), .out27(decoder_1_out27),
    .out28(decoder_1_out28), .out29(decoder_1_out29), .out30(decoder_1_out30), .out31(decoder_1_out31),
    .sel(RD));  // open: en
  Register #(.width(32)) register_1 (.D(WB), .Q(register_1_q), .clk(and_2_out));  // open: en, clr
  and and_2 (and_2_out, CLK, decoder_1_out0);
  Register #(.width(32)) register_2 (.D(WB), .Q(register_2_q), .clk(and_3_out));  // open: en, clr
  and and_3 (and_3_out, CLK, decoder_1_out1);
  Register #(.width(32)) register_3 (.D(WB), .Q(register_3_q), .clk(and_4_out));  // open: en, clr
  and and_4 (and_4_out, CLK, decoder_1_out2);
  Register #(.width(32)) register_4 (.D(WB), .Q(register_4_q), .clk(and_5_out));  // open: en, clr
  and and_5 (and_5_out, CLK, decoder_1_out3);
  Register #(.width(32)) register_5 (.D(WB), .Q(register_5_q), .clk(and_6_out));  // open: en, clr
  and and_6 (and_6_out, CLK, decoder_1_out4);
  Register #(.width(32)) register_6 (.D(WB), .Q(register_6_q), .clk(and_7_out));  // open: en, clr
  and and_7 (and_7_out, CLK, decoder_1_out5);
  Register #(.width(32)) register_7 (.D(WB), .Q(register_7_q), .clk(and_8_out));  // open: en, clr
  and and_8 (and_8_out, CLK, decoder_1_out6);
  Register #(.width(32)) register_8 (.D(WB), .Q(register_8_q), .clk(and_9_out), .clr(undriven));  // open: en
  and and_9 (and_9_out, CLK, decoder_1_out7);
  Register #(.width(32)) register_9 (.Q(register_9_q), .clk(and_10_out));  // open: D, en, clr
  and and_10 (and_10_out, CLK, decoder_1_out8);
  Register #(.width(32)) register_10 (.D(WB), .Q(register_10_q), .clk(and_11_out));  // open: en, clr
  and and_11 (and_11_out, CLK, decoder_1_out9);
  Register #(.width(32)) register_11 (.D(WB), .Q(register_11_q), .clk(and_12_out));  // open: en, clr
  and and_12 (and_12_out, CLK, decoder_1_out10);
  Register #(.width(32)) register_12 (.D(WB), .Q(register_12_q), .clk(and_13_out));  // open: en, clr
  and and_13 (and_13_out, CLK, decoder_1_out11);
  Register #(.width(32)) register_13 (.D(WB), .Q(register_13_q), .clk(and_14_out));  // open: en, clr
  and and_14 (and_14_out, CLK, decoder_1_out12);
  and and_15 (and_15_out, CLK, decoder_1_out13);
  and and_16 (and_16_out, CLK, decoder_1_out14);
  and and_17 (and_17_out, CLK, decoder_1_out15);
  Register #(.width(32)) register_14 (.D(WB), .Q(register_14_q), .clk(and_15_out));  // open: en, clr
  Register #(.width(32)) register_15 (.D(WB), .Q(register_15_q), .clk(and_16_out));  // open: en, clr
  Register #(.width(32)) register_16 (.D(WB), .Q(register_16_q), .clk(and_17_out));  // open: en, clr
  Register #(.width(32)) register_17 (.D(WB), .Q(register_17_q), .clk(and_18_out));  // open: en, clr
  and and_18 (and_18_out, CLK, decoder_1_out16);
  and and_19 (and_19_out, CLK, decoder_1_out17);
  and and_20 (and_20_out, CLK, decoder_1_out18);
  and and_21 (and_21_out, CLK, decoder_1_out19);
  and and_22 (and_22_out, CLK, decoder_1_out20);
  and and_23 (and_23_out, CLK, decoder_1_out21);
  and and_24 (and_24_out, CLK, decoder_1_out22);
  and and_25 (and_25_out, CLK, decoder_1_out23);
  and and_26 (and_26_out, CLK, decoder_1_out24);
  and and_27 (and_27_out, CLK, decoder_1_out25);
  and and_28 (and_28_out, CLK, decoder_1_out26);
  and and_29 (and_29_out, CLK, decoder_1_out27);
  and and_30 (and_30_out, CLK, decoder_1_out28);
  and and_31 (and_31_out, CLK, decoder_1_out29);
  and and_32 (and_32_out, CLK, decoder_1_out30);
  and and_33 (and_33_out, CLK, decoder_1_out31);
  Register #(.width(32)) register_18 (.D(WB), .Q(register_18_q), .clk(and_19_out));  // open: en, clr
  Register #(.width(32)) register_19 (.D(WB), .Q(register_19_q), .clk(and_20_out));  // open: en, clr
  Register #(.width(32)) register_20 (.D(WB), .Q(register_20_q), .clk(and_21_out));  // open: en, clr
  Register #(.width(32)) register_21 (.D(WB), .Q(register_21_q), .clk(and_22_out));  // open: en, clr
  Register #(.width(32)) register_22 (.D(WB), .Q(register_22_q), .clk(and_23_out));  // open: en, clr
  Register #(.width(32)) register_23 (.D(WB), .Q(register_23_q), .clk(and_24_out));  // open: en, clr
  Register #(.width(32)) register_24 (.D(WB), .Q(register_24_q), .clk(and_25_out));  // open: en, clr
  Register #(.width(32)) register_25 (.D(WB), .Q(register_25_q), .clk(and_26_out));  // open: en, clr
  Register #(.width(32)) register_26 (.D(WB), .Q(register_26_q), .clk(and_27_out));  // open: en, clr
  Register #(.width(32)) register_27 (.D(WB), .Q(register_27_q), .clk(and_28_out));  // open: en, clr
  Register #(.width(32)) register_28 (.D(WB), .Q(register_28_q), .clk(and_29_out));  // open: en, clr
  Register #(.width(32)) register_29 (.D(WB), .Q(register_29_q), .clk(and_30_out));  // open: en, clr
  Register #(.width(32)) register_30 (.D(WB), .Q(register_30_q), .clk(and_31_out));  // open: en, clr
  Register #(.width(32)) register_31 (.D(WB), .Q(register_31_q), .clk(and_32_out));  // open: en, clr
  Register #(.width(32)) register_32 (.D(WB), .Q(register_32_q), .clk(and_33_out));  // open: en, clr
  Multiplexer #(.select(5), .width(32)) multiplexer_1 (
    .in0(register_1_q), .in1(register_2_q), .in2(register_3_q), .in3(register_4_q), .in4(register_5_q),
    .in5(register_6_q), .in6(register_7_q), .in7(register_8_q), .in8(register_9_q), .in9(register_10_q),
    .in10(register_11_q), .in11(register_12_q), .in12(register_13_q), .in13(register_14_q),
    .in14(register_15_q), .in15(register_16_q), .in16(register_17_q), .in17(register_18_q),
    .in18(register_19_q), .in19(register_20_q), .in20(register_21_q), .in21(register_22_q),
    .in22(register_23_q), .in23(register_24_q), .in24(register_25_q), .in25(register_26_q),
    .in26(register_27_q), .in27(register_28_q), .in28(register_29_q), .in29(register_30_q),
    .in30(register_31_q), .in31(register_32_q), .out(out_7), .sel(RS_1));  // open: en
  Multiplexer #(.select(5), .width(32)) multiplexer_2 (
    .in0(register_1_q), .in1(register_2_q), .in2(register_3_q), .in3(register_4_q), .in4(register_5_q),
    .in5(register_6_q), .in6(register_7_q), .in7(register_8_q), .in8(register_9_q), .in9(register_10_q),
    .in10(register_11_q), .in11(register_12_q), .in12(register_13_q), .in13(register_14_q),
    .in14(register_15_q), .in15(register_16_q), .in16(register_17_q), .in17(register_18_q),
    .in18(register_19_q), .in19(register_20_q), .in20(register_21_q), .in21(register_22_q),
    .in22(register_23_q), .in23(register_24_q), .in24(register_25_q), .in25(register_26_q),
    .in26(register_27_q), .in27(register_28_q), .in28(register_29_q), .in29(register_30_q),
    .in30(register_31_q), .in31(register_32_q), .out(out_8), .sel(RS_2));  // open: en
endmodule

module Control_Unit (
  input  [6:0] in_1,
  output out_2,
  output out_3,
  output out_4,
  output out_5,
  output out_6,
  output out_7,
  output [1:0] out_8
);

  wire and_2_out, and_3_out, and_4_out, and_5_out, and_6_out, not_1_out, not_2_out, not_3_out;

  not not_1 (not_1_out, in_1[0]);
  and and_1 (out_8[0], in_1[0], in_1[1], ~in_1[2]);  // AND_Gate
  and and_2 (and_2_out, not_1_out, ~in_1[1]);  // AND_Gate
  and and_3 (and_3_out, not_1_out, in_1[4]);
  and and_4 (and_4_out, in_1[0], in_1[4]);
  and and_5 (and_5_out, in_1[1], ~in_1[2], ~in_1[4]);  // AND_Gate
  and and_6 (and_6_out, in_1[0], in_1[1], ~in_1[2]);  // AND_Gate
  and and_7 (out_4, ~in_1[0], ~in_1[1], ~in_1[2], ~in_1[3], ~in_1[4]);  // AND_Gate
  and and_8 (out_6, ~in_1[0], in_1[1], ~in_1[2], ~in_1[3], ~in_1[4]);  // AND_Gate
  and and_9 (out_7, in_1[0], in_1[1], ~in_1[2], ~in_1[3], ~in_1[4]);  // AND_Gate
  not not_2 (not_2_out, and_5_out);
  not not_3 (not_3_out, and_6_out);
  or or_1 (out_2, and_2_out, and_3_out, and_4_out);
  and and_10 (out_3, not_2_out, not_3_out);

  assign out_5 = out_4;
  assign out_8[1] = in_1[2];
endmodule

module ALU (
  input  [31:0] in_1,
  input  [31:0] in_2,
  input  [3:0] in_3,
  output [31:0] out_4,
  output out_5
);

  wire [4:0] bit_extender_1_out, bit_extender_2_out;
  wire [31:0] adder_1_out, and_1_out, or_1_out, shifter_1_out, shifter_2_out, subtractor_1_out, xor_1_out;

  Bit_Extender #(.in_width(32), .out_width(5)) bit_extender_1 (.in(in_2), .out(bit_extender_1_out));
  Bit_Extender #(.in_width(32), .out_width(5)) bit_extender_2 (.in(in_2), .out(bit_extender_2_out));
  Adder #(.width(32)) adder_1 (.a(in_2), .b(in_1), .out(adder_1_out));  // open: cin, cout
  Subtractor #(.width(32)) subtractor_1 (.a(in_2), .b(in_1), .out(subtractor_1_out));  // open: bin, bout
  Shifter #(.width(32)) shifter_1 (.in(in_2), .\dist (bit_extender_1_out), .out(shifter_1_out));
  Shifter #(.width(32), .shift("lr")) shifter_2 (.in(in_1), .\dist (bit_extender_2_out), .out(shifter_2_out));
  assign and_1_out = in_2 & in_1;  // AND_Gate and_1, 32 bits wide
  assign or_1_out = in_2 | in_1;  // OR_Gate or_1, 32 bits wide
  assign xor_1_out = in_2 ^ in_1;  // XOR_Gate xor_1, 32 bits wide
  Comparator #(.width(32)) comparator_1 (.a(in_1), .b(in_2), .eq(out_5));  // open: gt, lt
  Multiplexer #(.select(4), .width(32)) multiplexer_1 (
    .in0(and_1_out), .in1(or_1_out), .in2(adder_1_out), .in3(shifter_1_out), .in4(xor_1_out),
    .in5(shifter_2_out), .in6(subtractor_1_out), .out(out_4), .sel(in_3));  // open: in7, in8, in9, in10, in11, in12, in13, in14, in15, en
  Bit_Extender bit_extender_3 ();  // open: in, out
endmodule

module ALU_CTRL (
  input  [6:0] Function_7,
  input  [2:0] Function_3,
  input  [1:0] Input,
  output [3:0] ALU_SL
);

  wire and_1_out, and_2_out, and_3_out, and_4_out, and_5_out, and_6_out, or_1_out;

  and and_1 (and_1_out, ~Function_3[1], Function_3[0]);  // AND_Gate
  and and_2 (and_2_out, Function_3[2], Function_3[1], ~Function_3[0]);  // AND_Gate
  and and_3 (and_3_out, ~Function_3[2], ~Function_3[1]);  // AND_Gate
  and and_4 (and_4_out, ~Function_3[2], Function_3[0]);  // AND_Gate
  and and_5 (and_5_out, Input[1], ~Function_3[2], Function_7[1]);  // AND_Gate
  and and_6 (and_6_out, Input[1], Function_3[2], ~Function_3[1]);  // AND_Gate
  and and_7 (ALU_SL[3], Input[1], Function_3[2], Function_3[0], Function_7[1]);
  or or_1 (or_1_out, and_1_out, and_2_out);
  or or_2 (ALU_SL[1], ~Input[1], and_3_out, and_4_out);  // OR_Gate
  and and_8 (ALU_SL[0], Input[1], or_1_out);
  or or_3 (ALU_SL[2], Input[0], and_5_out, and_6_out);
endmodule
